# Fritzing sketch pitempmon (saved by Fritzing 0.9.3b)

parts:
  Raspberry_Pi_1 = Raspberry Pi 3 [part_number=RPI-3-V1.2]
  Q1 = Basic FET N-Channel [package="TO220 [THT]"]
  R1 = Resistor [tolerance=±5% resistance=2.2k package=THT]
  M1 = DC Motor

nets:
  N1: Raspberry_Pi_1.GPIO18, R1.Pin_0
  N2: Raspberry_Pi_1.GND, Q1.source
  N3: Raspberry_Pi_1.5V, M1.pin_1
  N4: Q1.gate, R1.Pin_1
  N5: Q1.drain, M1.pin_2

notes:
  gate
  drain
  source
  2n7000A
  fan
